# Fritzing sketch car-sketch (saved by Fritzing 0.9.4)

parts:
  DRL_R = DUO LED RG [package="5 mm [THT]"]
  DRL_L = DUO LED RG [package="5 mm [THT]"]
  Decoder = Resistor [tolerance=±5% resistance=220 package=THT]
  Decoder_2 = Resistor [tolerance=±5% resistance=220 package=THT]
  F1_-_3A = FUSE [package=fuse_5mm]
  BAT_-_12V = 12 battery [package=battery]

nets:
  N1: DRL_R.red_anode, Decoder_2.Pin_0
  N2: DRL_R.common_cathode, DRL_L.common_cathode, F1_-_3A.1
  N3: DRL_R.green_anode, DRL_L.red_anode, BAT_-_12V.-
  N4: DRL_L.green_anode, Decoder.Pin_1
  N5: F1_-_3A.2, BAT_-_12V.+

custom parts:
  12 battery: 12V lead acid type battery, like the Husqvarna YTH2448 12V 35AH battery. This is the mini version 1/4 the size of the actual battery to be closer to typical breadboard parts (around 2in wide rathher than 7in). The pads in pcb are sized to accomidate up to 14ga wire (as these batterys will deliver high currents.)
