# Fritzing sketch test-sketch (saved by Fritzing 0.9.4)
breadboards: 1

parts:
  J1 = Screw terminal - 2 pins [package=THT]
  J2 = Screw terminal - 2 pins [package=THT]
  6V = 4 x AAA Battery Mount
  6V_2 = 4 x AAA Battery Mount
  On/Off_SW = Toggle Switch spst [package=THT]
  DRL = smd LED [color="Red (633nm)" package="0603 [SMD]"]

nets:
  N1: J1.pin1, J2.pin1, 6V.-, DRL.cathode
  N2: J1.pin2, J2.pin2, On/Off_SW.L1, DRL.anode
  N3: 6V.+, 6V_2.-
  N4: 6V_2.+, On/Off_SW.COM

custom parts:
  Toggle Switch spst: Toggle Switch single pole single throw
